# Fritzing sketch proxSafe (saved by Fritzing 0.9.3b)
breadboards: 2

parts:
  MH-ET_LIVE_ESP32_DEVKIT1 = MH-ET LIVE ESP32 DEVKIT 38 pins
  HC-SR04_Sensor_1 = HC-SR04 Ultrasonic Distance Sensor
  HC-SR04_Sensor_2 = HC-SR04 Ultrasonic Distance Sensor
  HC-SR04_Sensor_3 = HC-SR04 Ultrasonic Distance Sensor
  HC-SR04_Sensor_4 = HC-SR04 Ultrasonic Distance Sensor
  J1 = Piezo Speaker

nets:
  N1: MH-ET_LIVE_ESP32_DEVKIT1.IO32, HC-SR04_Sensor_2.ECHO
  N2: MH-ET_LIVE_ESP32_DEVKIT1.IO33, HC-SR04_Sensor_2.TRIG
  N3: MH-ET_LIVE_ESP32_DEVKIT1.IO26, HC-SR04_Sensor_1.ECHO
  N4: MH-ET_LIVE_ESP32_DEVKIT1.IO27, HC-SR04_Sensor_1.TRIG
  GND: MH-ET_LIVE_ESP32_DEVKIT1.GND#58, HC-SR04_Sensor_1.GND, HC-SR04_Sensor_2.GND, HC-SR04_Sensor_3.GND, HC-SR04_Sensor_4.GND, J1.pin1
  VCC: MH-ET_LIVE_ESP32_DEVKIT1.5V, HC-SR04_Sensor_1.VCC, HC-SR04_Sensor_2.VCC, HC-SR04_Sensor_3.VCC, HC-SR04_Sensor_4.VCC
  N5: MH-ET_LIVE_ESP32_DEVKIT1.IO23, HC-SR04_Sensor_4.TRIG
  N6: MH-ET_LIVE_ESP32_DEVKIT1.IO22, HC-SR04_Sensor_4.ECHO
  N7: MH-ET_LIVE_ESP32_DEVKIT1.IO21, J1.pin2
  N8: MH-ET_LIVE_ESP32_DEVKIT1.IO5, HC-SR04_Sensor_3.TRIG
  N9: MH-ET_LIVE_ESP32_DEVKIT1.IO17, HC-SR04_Sensor_3.ECHO

custom parts:
  MH-ET LIVE ESP32 DEVKIT 38 pins: http://mh.nodebb.com/topic/2/mh-et-live-esp32-devkit
